# Fritzing sketch Weather Comparison (saved by Fritzing 0.9.1b)
breadboards: 1

parts:
  Raspberry_Pi1 = Raspberry Pi B+
  DS1 = DS18B20 1-Wire Temperature Sensor [part_number=DS18B20]
  R1 = Resistor [tolerance=±5% resistance=4.7k package=THT]

nets:
  N1: Raspberry_Pi1.GPIO4, DS1.DQ, R1.Pin_0
  N2: Raspberry_Pi1.GPIO17, DS1.VDD, R1.Pin_1
  GND: Raspberry_Pi1.GND, DS1.GND
